# Fritzing sketch Project_Circuit (saved by Fritzing 0.9.3b)
breadboards: 1

parts:
  Part1 = Arduino Uno (Rev3)
  J1 = Basic Servo
  M3 = DC Motor
  J4 = Infrared Proximity Sensor
  M1 = Dagu DGServo 9g (Top view) [part_number=RS001B]
  J2 = Infrared Proximity Sensor
  J3 = Infrared Proximity Sensor
  Part2 = Motor Driver 1A Dual TB6612FNG
  M2 = DC Motor
  BAT1 = Battery Holders [package=battery-aaa]
  BAT2 = Battery Holders [package=battery-aaa]
  BAT3 = Battery Holders [package=battery-aaa]
  BAT4 = Battery Holders [package=battery-aaa]
  BAT5 = Battery Holders [package=battery-aaa]
  BAT6 = Battery Holders [package=battery-aaa]

nets:
  N1: Part1.A1, J2.Vout
  N2: Part1.A3, J3.Vout
  N3: Part1.A5/SCL, J4.Vout
  N4: Part1.D8, Part2.BIN2
  N5: Part1.D9_PWM, Part2.STBY
  N6: Part1.D10_PWM/SS, J1.pulse
  N7: Part1.D11_PWM/MOSI, M1.pulse
  N8: Part1.D2, Part2.AIN1
  N9: Part1.D4, Part2.AIN2
  N10: Part1.D5_PWM, Part2.PWMA, Part2.PWMB
  N11: Part1.D7, Part2.BIN1
  VCC: Part1.5V, J1.vcc, J4.Vcc, M1.vcc, J2.Vcc, J3.Vcc, Part2.VCC, Part2.VM, BAT6.+
  GND: Part1.GND, J1.gnd, J4.GND, M1.gnd, J2.GND, J3.GND, Part2.GND, BAT1.-
  N12: M3.pin_1, Part2.B01
  N13: Part2.A02, M2.pin_2
  N14: Part2.A01, M2.pin_1
  N15: BAT1.+, BAT3.-
  N16: BAT2.-, BAT3.+
  N17: BAT2.+, BAT4.-
  N18: BAT4.+, BAT5.-
  N19: BAT5.+, BAT6.-
